// Logisim project main.circ as structural Verilog: 1 circuit, main circuit main
module main (
);

  wire button_2_out, button_3_out, button_4_out, button_out, cdm_16_1_p2, cdm_16_1_p3, cdm_16_1_p4,
       cdm_16_1_p5, cdm_16_1_p6, knopochki_1_p6, not_1_out, ram_1_p4;
  wire [3:0] knopochki_1_p5;
  wire [15:0] cdm_16_1_p1, cdm_16_1_p7, cdm_16_1_p8, controlled_buffer_2_out, display_controller_1_p1,
       display_controller_1_p2;

  // Debugger debugger_1: pin names not known
  Button button (.out(button_out));
  Button button_2 (.out(button_2_out));
  Button button_3 (.out(button_3_out));
  // CdM_16 cdm_16_1: pin names not known; wires that end beside it: cdm_16_1_p1, cdm_16_1_p2, cdm_16_1_p3, cdm_16_1_p4, cdm_16_1_p5, cdm_16_1_p6, cdm_16_1_p7, cdm_16_1_p8
  decoder decoder_1 (.in_1(cdm_16_1_p1));  // open: X_coord__bits_0_3, Y_coord__bits_4_7, pixel_state__bit_8, write__bit_9
  Button button_4 (.out(button_4_out));
  Clock clock_1 (.out(cdm_16_1_p2));
  DotMatrix #(.matrixcols(16), .matrixrows(16)) dotmatrix_1 (
    .col1(display_controller_1_p1), .col3(display_controller_1_p2));  // open: col0, col2, col4, col5, col6, col7, col8, col9, col10, col11, col12, col13, col14, col15
  // display_controller display_controller_1: pin names not known; wires that end beside it: display_controller_1_p1, display_controller_1_p2
  // knopochki knopochki_1: pin names not known; wires that end beside it: button_out, button_4_out, button_2_out, button_3_out, knopochki_1_p5, knopochki_1_p6
  assign cdm_16_1_p8 = cdm_16_1_p4 ? controlled_buffer_2_out : 16'bz;  // Controlled_Buffer controlled_buffer_1
  Register #(.width(4)) register_1 (.D(knopochki_1_p5), .clk(knopochki_1_p6));  // open: en, Q, clr
  assign controlled_buffer_2_out = not_1_out ? cdm_16_1_p7 : 16'bz;  // Controlled_Buffer controlled_buffer_2
  not not_1 (not_1_out, cdm_16_1_p4);
  // RAM ram_1: pin names not known; wires that end beside it: cdm_16_1_p6, cdm_16_1_p5, cdm_16_1_p3, ram_1_p4, cdm_16_1_p4, controlled_buffer_2_out
  Clock clock_2 (.out(ram_1_p4));

  // Notes on the sheet:
  //   Тут мы ставим кнопки для управления змеёй
  //   Тут мы ставим счётчик
endmodule
